// Logisim project project.circ as structural Verilog: 2 circuits, main circuit main
module main (
  input  TYPE,
  input  in_2,
  input  in_3,
  input  in_4,
  input  in_5,
  input  in_6,
  input  in_7,
  input  in_8,
  input  in_9,
  input  in_10,
  input  in_11,
  input  in_12,
  input  in_13,
  input  in_14,
  input  in_15,
  input  in_16,
  input  in_17
);

  wire and_1_out, and_2_out, and_3_out, and_4_out, and_5_out, and_6_out, and_7_out, and_8_out, and_9_out,
       and_10_out, and_11_out, and_12_out, and_13_out, and_14_out, and_15_out, and_16_out, and_17_out,
       and_18_out, and_19_out, and_20_out, and_21_out, and_22_out, and_23_out, clock_1_out, clock_2_out,
       not_1_out, not_2_out, not_3_out, not_4_out, not_5_out, not_6_out, not_7_out, not_8_out, not_9_out,
       not_10_out, not_11_out, not_12_out, not_13_out, not_14_out, not_15_out, not_16_out, not_17_out,
       not_18_out, not_19_out, not_20_out, not_21_out, not_22_out, not_23_out, not_24_out, not_25_out,
       not_26_out, not_27_out, not_28_out, not_29_out, not_30_out, not_31_out, or_1_out, or_2_out, or_3_out,
       or_4_out, or_5_out, register_1_q, register_2_q, register_3_q, register_4_q, register_5_q,
       register_6_q, register_7_q, register_8_q;

  not not_1 (not_1_out, TYPE);
  not not_2 (not_2_out, register_6_q);
  not not_3 (not_3_out, register_7_q);
  not not_4 (not_4_out, TYPE);
  not not_5 (not_5_out, register_5_q);
  not not_6 (not_6_out, register_5_q);
  not not_7 (not_7_out, register_6_q);
  not not_8 (not_8_out, register_7_q);
  not not_9 (not_9_out, register_8_q);
  not not_10 (not_10_out, register_5_q);
  not not_11 (not_11_out, register_7_q);
  not not_12 (not_12_out, register_8_q);
  not not_13 (not_13_out, register_6_q);
  not not_14 (not_14_out, register_5_q);
  not not_15 (not_15_out, register_6_q);
  not not_16 (not_16_out, register_8_q);
  not not_17 (not_17_out, register_7_q);
  not not_18 (not_18_out, register_5_q);
  not not_19 (not_19_out, register_6_q);
  not not_20 (not_20_out, register_7_q);
  not not_21 (not_21_out, TYPE);
  not not_22 (not_22_out, register_6_q);
  not not_23 (not_23_out, TYPE);
  not not_24 (not_24_out, register_7_q);
  not not_25 (not_25_out, TYPE);
  not not_26 (not_26_out, register_6_q);
  not not_27 (not_27_out, register_8_q);
  not not_28 (not_28_out, register_6_q);
  not not_29 (not_29_out, register_7_q);
  and and_1 (and_1_out, not_1_out, not_2_out, not_3_out);
  and and_2 (and_2_out, not_4_out, not_5_out, register_8_q);
  and and_3 (and_3_out, not_6_out, register_6_q, register_7_q);
  and and_4 (and_4_out, register_5_q, not_7_out);
  and and_5 (and_5_out, register_5_q, not_8_out);
  and and_6 (and_6_out, register_5_q, not_9_out);
  and and_7 (and_7_out, not_10_out, register_6_q);
  and and_8 (and_8_out, register_6_q, not_11_out);
  and and_9 (and_9_out, register_6_q, not_12_out);
  and and_10 (and_10_out, TYPE, not_13_out);
  and and_11 (and_11_out, not_14_out, register_7_q);
  and and_12 (and_12_out, not_15_out, register_7_q);
  and and_13 (and_13_out, register_7_q, not_16_out);
  and and_14 (and_14_out, TYPE, register_6_q, not_17_out);
  and and_15 (and_15_out, not_18_out, register_8_q);
  and and_16 (and_16_out, not_19_out, register_8_q);
  and and_17 (and_17_out, not_20_out, register_8_q);
  and and_18 (and_18_out, not_21_out, not_22_out, register_7_q);
  and and_19 (and_19_out, not_23_out, register_6_q, not_24_out);
  and and_20 (and_20_out, not_25_out, register_5_q, not_26_out);
  and and_21 (and_21_out, register_5_q, register_6_q, register_7_q, not_27_out);
  not not_30 (not_30_out, register_5_q);
  not not_31 (not_31_out, register_8_q);
  and and_22 (and_22_out, TYPE, not_28_out);
  and and_23 (and_23_out, TYPE, not_29_out);
  or or_1 (or_1_out, and_1_out, and_2_out, and_3_out, and_4_out, and_5_out, and_6_out);
  or or_2 (or_2_out, and_7_out, and_8_out, and_9_out, and_10_out);
  or or_3 (or_3_out, and_11_out, and_12_out, and_13_out, and_14_out);
  or or_4 (or_4_out, and_15_out, and_16_out, and_17_out, and_18_out, and_19_out, and_20_out, and_21_out);
  or or_5 (or_5_out, not_30_out, not_31_out, and_22_out, and_23_out);
  Register #(.width(1)) register_1 (.D(or_1_out), .en(in_3), .Q(register_1_q), .clk(clock_1_out), .clr(in_5));
  Register #(.width(1)) register_2 (.D(or_2_out), .en(in_7), .Q(register_2_q), .clk(clock_1_out));  // open: clr
  Register #(.width(1)) register_3 (.D(or_3_out), .en(in_10), .Q(register_3_q), .clk(clock_1_out), .clr(in_12));
  Register #(.width(1)) register_4 (.D(or_4_out), .en(in_14), .Q(register_4_q), .clk(clock_1_out), .clr(in_17));
  Register #(.width(1)) register_5 (.D(register_1_q), .en(in_2), .Q(register_5_q), .clk(clock_2_out), .clr(in_4));
  Register #(.width(1)) register_6 (.D(register_2_q), .en(in_6), .Q(register_6_q), .clk(clock_2_out), .clr(in_9));
  Register #(.width(1)) register_7 (.D(register_3_q), .en(in_11), .Q(register_7_q), .clk(clock_2_out), .clr(in_13));
  Register #(.width(1)) register_8 (.D(register_4_q), .en(in_15), .Q(register_8_q), .clk(clock_2_out));  // open: clr
  Clock #(.highDuration(8), .lowDuration(8)) clock_1 (.out(clock_1_out));
  Clock clock_2 (.out(clock_2_out));
  LED PL1 (.in(or_1_out));
  LED led_1 (.in(or_2_out));
  LED led_2 (.in(or_3_out));
  LED led_3 (.in(or_4_out));
  LED led_4 (.in(or_5_out));

  // Notes on the sheet:
  //   1 FIRST CLICK THE CLOCK 1 TO STORE THE PRESENT OUTPUT;
  //   2 NOW ENTER THE TYPE OF TRAIN YOU WANT TO ENTER .       
  //   INSTRUCTIONS :-
  //   3 NOW ON THE CLK2 AND THEN OFF IT AGAIN ,YOU WILL GET THE CURRENT CONDITION OF THE TRACKS
  //     AND THEN SWITCH OF THE CLK1
  //   CLK 1
  //   CLK 2
  //   PL1
  //   PL2
  //   PL3
  //   PL4
  //   VALID
endmodule

module PROJ (
  input  T,
  input  A,
  input  B,
  input  C,
  input  D,
  output E,
  output F,
  output G,
  output H,
  output V
);

  wire and_1_out, and_2_out, and_3_out, and_4_out, and_5_out, and_6_out, and_7_out, and_8_out, and_9_out,
       and_10_out, and_11_out, and_12_out, and_13_out, and_14_out, and_15_out, and_16_out, and_17_out,
       and_18_out, and_19_out, and_20_out, and_21_out, and_22_out, and_23_out, not_1_out, not_2_out,
       not_3_out, not_4_out, not_5_out, not_6_out, not_7_out, not_8_out, not_9_out, not_10_out, not_11_out,
       not_12_out, not_13_out, not_14_out, not_15_out, not_16_out, not_17_out, not_18_out, not_19_out,
       not_20_out, not_21_out, not_22_out, not_23_out, not_24_out, not_25_out, not_26_out, not_27_out,
       not_28_out, not_29_out, not_30_out, not_31_out;

  not not_1 (not_1_out, T);
  not not_2 (not_2_out, B);
  not not_3 (not_3_out, C);
  not not_4 (not_4_out, T);
  not not_5 (not_5_out, A);
  not not_6 (not_6_out, A);
  not not_7 (not_7_out, B);
  not not_8 (not_8_out, C);
  not not_9 (not_9_out, D);
  not not_10 (not_10_out, A);
  not not_11 (not_11_out, C);
  not not_12 (not_12_out, D);
  not not_13 (not_13_out, B);
  not not_14 (not_14_out, A);
  not not_15 (not_15_out, B);
  not not_16 (not_16_out, D);
  not not_17 (not_17_out, C);
  not not_18 (not_18_out, A);
  not not_19 (not_19_out, B);
  not not_20 (not_20_out, C);
  not not_21 (not_21_out, T);
  not not_22 (not_22_out, B);
  not not_23 (not_23_out, T);
  not not_24 (not_24_out, C);
  not not_25 (not_25_out, T);
  not not_26 (not_26_out, B);
  not not_27 (not_27_out, D);
  not not_28 (not_28_out, B);
  not not_29 (not_29_out, C);
  and and_1 (and_1_out, not_1_out, not_2_out, not_3_out);
  and and_2 (and_2_out, not_4_out, not_5_out, D);
  and and_3 (and_3_out, not_6_out, B, C);
  and and_4 (and_4_out, A, not_7_out);
  and and_5 (and_5_out, A, not_8_out);
  and and_6 (and_6_out, A, not_9_out);
  and and_7 (and_7_out, not_10_out, B);
  and and_8 (and_8_out, B, not_11_out);
  and and_9 (and_9_out, B, not_12_out);
  and and_10 (and_10_out, T, not_13_out);
  and and_11 (and_11_out, not_14_out, C);
  and and_12 (and_12_out, not_15_out, C);
  and and_13 (and_13_out, C, not_16_out);
  and and_14 (and_14_out, T, B, not_17_out);
  and and_15 (and_15_out, not_18_out, D);
  and and_16 (and_16_out, not_19_out, D);
  and and_17 (and_17_out, not_20_out, D);
  and and_18 (and_18_out, not_21_out, not_22_out, C);
  and and_19 (and_19_out, not_23_out, B, not_24_out);
  and and_20 (and_20_out, not_25_out, A, not_26_out);
  and and_21 (and_21_out, A, B, C, not_27_out);
  not not_30 (not_30_out, A);
  not not_31 (not_31_out, D);
  and and_22 (and_22_out, T, not_28_out);
  and and_23 (and_23_out, T, not_29_out);
  or or_1 (E, and_1_out, and_2_out, and_3_out, and_4_out, and_5_out, and_6_out);
  or or_2 (F, and_7_out, and_8_out, and_9_out, and_10_out);
  or or_3 (G, and_11_out, and_12_out, and_13_out, and_14_out);
  or or_4 (H, and_15_out, and_16_out, and_17_out, and_18_out, and_19_out, and_20_out, and_21_out);
  or or_5 (V, not_30_out, not_31_out, and_22_out, and_23_out);
endmodule
