// Logisim project project.circ as structural Verilog: 1 circuit, main circuit main
module main (
  input  in_1,
  input  in_2,
  input  in_3,
  input  in_4
);

  wire and_1_out, and_2_out, and_3_out, clock_1_out, d_ff_1_q, d_ff_2_q, not_1_out, not_2_out, not_3_out,
       or_1_out, or_2_out, or_3_out, xor_1_out;

  Clock clock_1 (.out(clock_1_out));
  and and_1 (and_1_out, not_1_out, not_3_out);
  xor xor_1 (xor_1_out, d_ff_2_q, d_ff_1_q);
  not not_1 (not_1_out, in_1);
  or or_1 (or_1_out, xor_1_out, and_1_out);
  D_Flip_Flop d_ff_1 (
    .clk(clock_1_out), .D(or_1_out), .Q(d_ff_1_q), .preset(in_2), .en(in_3), .reset(in_4));  // open: Qn
  not not_2 (not_2_out, d_ff_1_q);
  and and_2 (and_2_out, not_3_out, in_1);
  and and_3 (and_3_out, not_2_out, d_ff_2_q);
  D_Flip_Flop d_ff_2 (
    .clk(clock_1_out), .D(or_2_out), .Q(d_ff_2_q), .preset(in_2), .en(in_3), .reset(in_4));  // open: Qn
  not not_3 (not_3_out, d_ff_2_q);
  or or_2 (or_2_out, and_3_out, and_2_out);
  or or_3 (or_3_out, not_2_out, and_2_out);
  LED led_1 (.in(d_ff_1_q));
  LED led_2 (.in(d_ff_2_q));
  LED led_3 (.in(or_3_out));
endmodule
